// Logisim project progetto.circ as structural Verilog: 8 circuits, main circuit main
module main (
  output [4:0] out_1,
  output [4:0] out_2,
  output [4:0] out_3,
  output [4:0] out_4
);

  wire _0_out, _1_out, _2_out, _3_out, _4_out, _5_out, _6_out, _7_out, _8_out, _9_out, and_1_out,
       button_2_out, button_out, clock_1_out, keypad_1_clicked, minus_1_out_2, not_1_out, not_2_out,
       not_3_out, not_4_out, not_5_out, OK_out, or_1_out;
  wire [1:0] counter_1_q;
  wire [3:0] keypad_1_b0;
  wire [4:0] calcolo_1_out_5, counter_2_q, demultiplexer_1_out0, multiplexer_1_out, negativator_1_out_2,
       register_1_q;
  wire [31:0] decoder_1_out0;

  Button _8 (.out(_8_out));
  Button _7 (.out(_7_out));
  Button _4 (.out(_4_out));
  Button _5 (.out(_5_out));
  Button _1 (.out(_1_out));
  Button _2 (.out(_2_out));
  Button _0 (.out(_0_out));
  Button OK (.out(OK_out));
  Button button (.out(button_out));
  DotMatrix #(.matrixcols(32), .matrixrows(32)) dotmatrix_1 (
    .col0(decoder_1_out0), .col1(decoder_1_out0), .col2(decoder_1_out0), .col3(decoder_1_out0),
    .col4(decoder_1_out0), .col5(decoder_1_out0), .col6(decoder_1_out0), .col7(decoder_1_out0),
    .col8(decoder_1_out0), .col9(decoder_1_out0), .col10(decoder_1_out0), .col11(decoder_1_out0),
    .col12(decoder_1_out0), .col13(decoder_1_out0), .col14(decoder_1_out0));  // open: col15, col16, col17, col18, col19, col20, col21, col22, col23, col24, col25, col26, col27, col28, col29, col30, col31
  Button _9 (.out(_9_out));
  Button _6 (.out(_6_out));
  Button _3 (.out(_3_out));
  Button button_2 (.out(button_2_out));
  or or_1 (or_1_out, OK_out, button_out);
  keypad keypad_1 (
    ._0(_0_out), ._1(_1_out), ._3(_3_out), ._2(_2_out), ._5(_5_out), ._4(_4_out), ._7(_7_out), ._6(_6_out),
    .b2_2(keypad_1_b0[2]), .b1(keypad_1_b0[1]), .b0(keypad_1_b0[0]), ._8(_8_out), ._9(_9_out),
    .b2(keypad_1_b0[3]), .clicked(keypad_1_clicked));
  LED meno (.in(minus_1_out_2));
  minus minus_1 (.in_1(button_2_out), .out_2(minus_1_out_2));
  Counter #(.width(2), .max('h2), .trigger("falling")) counter_1 (
    .Q(counter_1_q), .clk(or_1_out));  // open: load, D, count, carry, clr
  Multiplexer #(.width(5)) multiplexer_1 (
    .in0({1'b0, keypad_1_b0}), .in1(negativator_1_out_2), .out(multiplexer_1_out), .sel(minus_1_out_2));  // open: en
  negativator negativator_1 (.in_1({1'b0, keypad_1_b0}), .out_2(negativator_1_out_2));
  Counter #(.width(5), .max('h1f)) counter_2 (.Q(counter_2_q), .clk(clock_1_out));  // open: load, D, count, carry, clr
  Clock clock_1 (.out(clock_1_out));
  not not_1 (not_1_out, counter_2_q[0]);
  not not_2 (not_2_out, counter_2_q[2]);
  not not_3 (not_3_out, counter_2_q[4]);
  not not_4 (not_4_out, counter_2_q[3]);
  not not_5 (not_5_out, counter_2_q[1]);
  memory memory_1 (
    .in_1(multiplexer_1_out), .in_2(keypad_1_clicked), .in_3(OK_out), .in_4(counter_1_q), .out_5(out_1),
    .out_6(out_2), .out_7(out_3), .out_8(out_4));
  and and_1 (and_1_out, not_1_out, not_5_out, not_2_out, not_4_out, not_3_out, clock_1_out);
  Decoder #(.select(5)) decoder_1 (
    .out0(decoder_1_out0[0]), .out1(decoder_1_out0[1]), .out2(decoder_1_out0[2]), .out3(decoder_1_out0[3]),
    .out4(decoder_1_out0[4]), .out5(decoder_1_out0[5]), .out6(decoder_1_out0[6]), .out7(decoder_1_out0[7]),
    .out8(decoder_1_out0[8]), .out9(decoder_1_out0[9]), .sel(register_1_q));  // open: out10, out11, out12, out13, out14, out15, out16, out17, out18, out19, out20, out21, out22, out23, out24, out25, out26, out27, out28, out29, out30, out31, en
  calcolo calcolo_1 (.c_x_2(out_1), .c_x(out_2), .q(out_3), .out_5(calcolo_1_out_5), .x(counter_2_q));
  Register #(.width(5)) register_1 (.D(demultiplexer_1_out0), .Q(register_1_q), .clk(and_1_out));  // open: en, clr
  Demultiplexer #(.select(5), .width(5)) demultiplexer_1 (
    .out0(demultiplexer_1_out0), .in(calcolo_1_out_5), .sel(counter_2_q));  // open: out1, out2, out3, out4, out5, out6, out7, out8, out9, out10, out11, out12, out13, out14, out15, out16, out17, out18, out19, out20, out21, out22, out23, out24, out25, out26, out27, out28, out29, out30, out31, en
endmodule

module keypad (
  input  _0,
  input  _1,
  input  _3,
  input  _2,
  input  _5,
  input  _4,
  input  _7,
  input  _6,
  input  _9,
  input  _8,
  output clicked,
  output b2,
  output b2_2,
  output b1,
  output b0
);

  or or_1 (b0, _1, _9, _3, _5, _7);
  or or_2 (b1, _3, _2, _7, _6);
  or or_3 (b2_2, _6, _5, _7, _4);
  or or_4 (b2, _9, _8);
  or or_5 (clicked, _0, b0, b1, b2_2, b2);
endmodule

module negativator (
  input  [4:0] in_1,
  output [4:0] out_2
);

  wire [4:0] not_1_out;

  assign not_1_out = ~in_1;  // NOT_Gate not_1, 5 bits wide
  Adder #(.width(5)) adder_1 (.a(not_1_out), .b(5'b00001), .out(out_2));  // open: cin, cout
endmodule

module memory (
  input  [4:0] in_1,
  input  in_2,
  input  in_3,
  input  [1:0] in_4,
  output [4:0] out_5,
  output [4:0] out_6,
  output [4:0] out_7,
  output [4:0] out_8
);

  wire demultiplexer_2_out0, demultiplexer_2_out1, demultiplexer_2_out2, demultiplexer_2_out3;
  wire [4:0] d_ff_1_q, demultiplexer_1_out0, demultiplexer_1_out1, demultiplexer_1_out2, demultiplexer_1_out3;

  D_Flip_Flop #(.trigger("high")) d_ff_1 (.clk(in_2), .D(in_1[0]), .Q(d_ff_1_q[0]));  // open: Qn, preset, en, reset
  D_Flip_Flop #(.trigger("high")) d_ff_2 (.clk(in_2), .D(in_1[1]), .Q(d_ff_1_q[1]));  // open: Qn, preset, en, reset
  D_Flip_Flop #(.trigger("high")) d_ff_3 (.clk(in_2), .D(in_1[2]), .Q(d_ff_1_q[2]));  // open: Qn, preset, en, reset
  D_Flip_Flop #(.trigger("high")) d_ff_4 (.clk(in_2), .D(in_1[3]), .Q(d_ff_1_q[3]));  // open: Qn, preset, en, reset
  D_Flip_Flop #(.trigger("high")) d_ff_5 (.clk(in_2), .D(in_1[4]), .Q(d_ff_1_q[4]));  // open: Qn, preset, en, reset
  Demultiplexer #(.select(2), .width(5)) demultiplexer_1 (
    .out0(demultiplexer_1_out0), .out1(demultiplexer_1_out1), .out2(demultiplexer_1_out2),
    .out3(demultiplexer_1_out3), .in(d_ff_1_q), .sel(in_4));  // open: en
  Demultiplexer #(.select(2)) demultiplexer_2 (
    .out0(demultiplexer_2_out0), .out1(demultiplexer_2_out1), .out2(demultiplexer_2_out2),
    .out3(demultiplexer_2_out3), .in(in_3), .sel(in_4));  // open: en
  Register #(.width(5), .trigger("high")) register_1 (
    .D(demultiplexer_1_out0), .Q(out_5), .clk(demultiplexer_2_out0));  // open: en, clr
  Register #(.width(5), .trigger("high")) register_2 (
    .D(demultiplexer_1_out1), .Q(out_6), .clk(demultiplexer_2_out1));  // open: en, clr
  Register #(.width(5), .trigger("high")) register_3 (
    .D(demultiplexer_1_out2), .Q(out_7), .clk(demultiplexer_2_out2));  // open: en, clr
  Register #(.width(5), .trigger("high")) register_4 (
    .D(demultiplexer_1_out3), .Q(out_8), .clk(demultiplexer_2_out3));  // open: en, clr
endmodule

module minus (
  input  in_1,
  output out_2
);

  wire and_1_out, d_ff_1_qn;

  and and_1 (and_1_out, in_1, d_ff_1_qn);
  D_Flip_Flop #(.trigger("falling")) d_ff_1 (
    .clk(in_1), .D(and_1_out), .Q(out_2), .Qn(d_ff_1_qn));  // open: preset, en, reset
endmodule

module calcolo (
  input  [4:0] c_x_2,
  input  [4:0] c_x,
  input  [4:0] q,
  input  [4:0] x,
  output [4:0] out_5
);

  wire adder_1_cout;
  wire [4:0] adder_1_out, multiplier_1_out, multiplier_2_cout, multiplier_2_out, multiplier_3_out;

  Multiplier #(.width(5)) multiplier_1 (.a(c_x), .b(x), .out(multiplier_1_out));  // open: cin, cout
  Multiplier #(.width(5)) multiplier_2 (
    .a(c_x_2), .b(x), .out(multiplier_2_out), .cout(multiplier_2_cout));  // open: cin
  Multiplier #(.width(5)) multiplier_3 (
    .a(multiplier_2_out), .b(x), .out(multiplier_3_out), .cin(multiplier_2_cout));  // open: cout
  Adder #(.width(5)) adder_1 (
    .a(multiplier_3_out), .b(multiplier_1_out), .out(adder_1_out), .cout(adder_1_cout));  // open: cin
  Adder #(.width(5)) adder_2 (.a(q), .b(adder_1_out), .out(out_5), .cin(adder_1_cout));  // open: cout
endmodule

module x_selector (
  input  [4:0] y,
  input  [4:0] x,
  input  CLK
);

  wire [4:0] dmx0, dmx1, dmx2, dmx3, dmx4, dmx5, dmx6, dmx7, dmx8, dmx9, dmx10, dmx11, dmx12, dmx13, dmx14,
       dmx15, dmx16, dmx17, dmx18, dmx19, dmx20, dmx21, dmx22, dmx23, dmx24, dmx25, dmx26, dmx27, dmx28,
       dmx29, dmx30, dmx31;
  wire [31:0] decoder_1_out0;

  Decoder #(.select(5)) decoder_1 (
    .out0(decoder_1_out0[0]), .out1(decoder_1_out0[1]), .out2(decoder_1_out0[2]), .out3(decoder_1_out0[3]),
    .out4(decoder_1_out0[4]), .out5(decoder_1_out0[5]), .out6(decoder_1_out0[6]), .out7(decoder_1_out0[7]),
    .out8(decoder_1_out0[8]), .out9(decoder_1_out0[9]), .out10(decoder_1_out0[10]),
    .out11(decoder_1_out0[11]), .out12(decoder_1_out0[12]), .out13(decoder_1_out0[13]),
    .out14(decoder_1_out0[14]), .out15(decoder_1_out0[15]), .out16(decoder_1_out0[16]),
    .out17(decoder_1_out0[17]), .out18(decoder_1_out0[18]), .out19(decoder_1_out0[19]),
    .out20(decoder_1_out0[20]), .out21(decoder_1_out0[21]), .out22(decoder_1_out0[22]),
    .out23(decoder_1_out0[23]), .out24(decoder_1_out0[24]), .out25(decoder_1_out0[25]),
    .out26(decoder_1_out0[26]), .out27(decoder_1_out0[27]), .out28(decoder_1_out0[28]),
    .out29(decoder_1_out0[29]), .out30(decoder_1_out0[30]), .out31(decoder_1_out0[31]), .sel(dmx0));  // open: en
  Demultiplexer #(.select(5), .width(5)) demultiplexer_1 (
    .out0(dmx0), .out1(dmx1), .out2(dmx2), .out3(dmx3), .out4(dmx4), .out5(dmx5), .out6(dmx6), .out7(dmx7),
    .out8(dmx8), .out9(dmx9), .out10(dmx10), .out11(dmx11), .out12(dmx12), .out13(dmx13), .out14(dmx14),
    .out15(dmx15), .out16(dmx16), .out17(dmx17), .out18(dmx18), .out19(dmx19), .out20(dmx20), .out21(dmx21),
    .out22(dmx22), .out23(dmx23), .out24(dmx24), .out25(dmx25), .out26(dmx26), .out27(dmx27), .out28(dmx28),
    .out29(dmx29), .out30(dmx30), .out31(dmx31), .in(y), .sel(x));  // open: en
endmodule

module xy_selector (
  input  [4:0] x,
  input  [4:0] y,
  output [31:0] x0_output,
  output [31:0] x16_output,
  output [31:0] x1_output,
  output [31:0] x17_output,
  output [31:0] x2_output,
  output [31:0] x18_output,
  output [31:0] x3_output,
  output [31:0] x19_output,
  output [31:0] x4_output,
  output [31:0] x5_output,
  output [31:0] x6_output,
  output [31:0] x7_output,
  output [31:0] x8_output,
  output [31:0] x9_output,
  output [31:0] x10_output,
  output [31:0] x11_output,
  output [31:0] x12_output,
  output [31:0] x13_output,
  output [31:0] x14_output,
  output [31:0] x15_output
);

  wire and_1_out, and_2_out, and_3_out, and_4_out, and_5_out, and_6_out, and_7_out, and_8_out, and_9_out,
       and_10_out, and_11_out, and_12_out, and_13_out, and_14_out, and_15_out, and_16_out, and_17_out,
       and_18_out, and_19_out, and_20_out, CLK;
  wire [31:0] decoder_1_out0;

  Clock clock_1 (.out(CLK));
  Decoder #(.select(5)) decoder_1 (
    .out0(decoder_1_out0[0]), .out1(decoder_1_out0[1]), .out2(decoder_1_out0[2]), .out3(decoder_1_out0[3]),
    .out4(decoder_1_out0[4]), .out5(decoder_1_out0[5]), .out6(decoder_1_out0[6]), .out7(decoder_1_out0[7]),
    .out8(decoder_1_out0[8]), .out9(decoder_1_out0[9]), .out10(decoder_1_out0[10]),
    .out11(decoder_1_out0[11]), .out12(decoder_1_out0[12]), .out13(decoder_1_out0[13]),
    .out14(decoder_1_out0[14]), .out15(decoder_1_out0[15]), .out16(decoder_1_out0[16]),
    .out17(decoder_1_out0[17]), .out18(decoder_1_out0[18]), .out19(decoder_1_out0[19]),
    .out20(decoder_1_out0[20]), .out21(decoder_1_out0[21]), .out22(decoder_1_out0[22]),
    .out23(decoder_1_out0[23]), .out24(decoder_1_out0[24]), .out25(decoder_1_out0[25]),
    .out26(decoder_1_out0[26]), .out27(decoder_1_out0[27]), .out28(decoder_1_out0[28]),
    .out29(decoder_1_out0[29]), .out30(decoder_1_out0[30]), .out31(decoder_1_out0[31]), .sel(y));  // open: en
  Register #(.width(32), .trigger("high")) x16 (.D(decoder_1_out0), .Q(x16_output), .clk(and_1_out));  // open: en, clr
  and and_1 (and_1_out, x[4], ~x[3], ~x[2], ~x[1], ~x[0], CLK);  // AND_Gate
  Register #(.width(32), .trigger("high")) x17 (.D(decoder_1_out0), .Q(x17_output), .clk(and_2_out));  // open: en, clr
  and and_2 (and_2_out, x[4], ~x[3], ~x[2], ~x[1], x[0], CLK);  // AND_Gate
  Register #(.width(32), .trigger("high")) x18 (.D(decoder_1_out0), .Q(x18_output), .clk(and_3_out));  // open: en, clr
  and and_3 (and_3_out, x[4], ~x[3], ~x[2], x[1], ~x[0], CLK);  // AND_Gate
  Register #(.width(32), .trigger("high")) x19 (.D(decoder_1_out0), .Q(x19_output), .clk(and_4_out));  // open: en, clr
  and and_4 (and_4_out, x[4], ~x[3], ~x[2], x[1], x[0], CLK);  // AND_Gate
  Register #(.width(32), .trigger("high")) x0 (.D(decoder_1_out0), .Q(x0_output), .clk(and_5_out));  // open: en, clr
  and and_5 (and_5_out, ~x[4], ~x[3], ~x[2], ~x[1], ~x[0], CLK);  // AND_Gate
  Register #(.width(32), .trigger("high")) x1 (.D(decoder_1_out0), .Q(x1_output), .clk(and_6_out));  // open: en, clr
  and and_6 (and_6_out, ~x[4], ~x[3], ~x[2], ~x[1], x[0], CLK);  // AND_Gate
  Register #(.width(32), .trigger("high")) x2 (.D(decoder_1_out0), .Q(x2_output), .clk(and_7_out));  // open: en, clr
  and and_7 (and_7_out, ~x[4], ~x[3], ~x[2], x[1], ~x[0], CLK);  // AND_Gate
  Register #(.width(32), .trigger("high")) x3 (.D(decoder_1_out0), .Q(x3_output), .clk(and_8_out));  // open: en, clr
  and and_8 (and_8_out, ~x[4], ~x[3], ~x[2], x[1], x[0], CLK);  // AND_Gate
  Register #(.width(32), .trigger("high")) x4 (.D(decoder_1_out0), .Q(x4_output), .clk(and_9_out));  // open: en, clr
  and and_9 (and_9_out, ~x[4], ~x[3], x[2], ~x[1], ~x[0], CLK);  // AND_Gate
  Register #(.width(32), .trigger("high")) x5 (.D(decoder_1_out0), .Q(x5_output), .clk(and_10_out));  // open: en, clr
  and and_10 (and_10_out, ~x[4], ~x[3], x[2], ~x[1], x[0], CLK);  // AND_Gate
  Register #(.width(32), .trigger("high")) x6 (.D(decoder_1_out0), .Q(x6_output), .clk(and_11_out));  // open: en, clr
  and and_11 (and_11_out, ~x[4], ~x[3], x[2], x[1], ~x[0], CLK);  // AND_Gate
  Register #(.width(32), .trigger("high")) x7 (.D(decoder_1_out0), .Q(x7_output), .clk(and_12_out));  // open: en, clr
  and and_12 (and_12_out, ~x[4], ~x[3], x[2], x[1], x[0], CLK);  // AND_Gate
  Register #(.width(32), .trigger("high")) x8 (.D(decoder_1_out0), .Q(x8_output), .clk(and_13_out));  // open: en, clr
  and and_13 (and_13_out, ~x[4], x[3], ~x[2], ~x[1], ~x[0], CLK);  // AND_Gate
  Register #(.width(32), .trigger("high")) x9 (.D(decoder_1_out0), .Q(x9_output), .clk(and_14_out));  // open: en, clr
  and and_14 (and_14_out, ~x[4], x[3], ~x[2], ~x[1], x[0], CLK);  // AND_Gate
  Register #(.width(32), .trigger("high")) x10 (.D(decoder_1_out0), .Q(x10_output), .clk(and_15_out));  // open: en, clr
  and and_15 (and_15_out, ~x[4], x[3], ~x[2], x[1], ~x[0], CLK);  // AND_Gate
  Register #(.width(32), .trigger("high")) x11 (.D(decoder_1_out0), .Q(x11_output), .clk(and_16_out));  // open: en, clr
  and and_16 (and_16_out, ~x[4], x[3], ~x[2], x[1], x[0], CLK);  // AND_Gate
  Register #(.width(32), .trigger("high")) x12 (.D(decoder_1_out0), .Q(x12_output), .clk(and_17_out));  // open: en, clr
  and and_17 (and_17_out, ~x[4], x[3], x[2], ~x[1], ~x[0], CLK);  // AND_Gate
  Register #(.width(32), .trigger("high")) x13 (.D(decoder_1_out0), .Q(x13_output), .clk(and_18_out));  // open: en, clr
  and and_18 (and_18_out, ~x[4], x[3], x[2], ~x[1], x[0], CLK);  // AND_Gate
  Register #(.width(32), .trigger("high")) x14 (.D(decoder_1_out0), .Q(x14_output), .clk(and_19_out));  // open: en, clr
  and and_19 (and_19_out, ~x[4], x[3], x[2], x[1], ~x[0], CLK);  // AND_Gate
  Register #(.width(32), .trigger("high")) x15 (.D(decoder_1_out0), .Q(x15_output), .clk(and_20_out));  // open: en, clr
  and and_20 (and_20_out, ~x[4], x[3], x[2], x[1], x[0], CLK);  // AND_Gate
endmodule
